# Fritzing sketch rotation-meter (saved by Fritzing 0.9.3b)
circuit board: 6.5cm x 4.4cm
breadboards: 1

parts:
  U1 = QRD1114 [package=qrd1114]
  R1 = Resistor [tolerance=±5% resistance=330 package=THT]
  R2 = Resistor [tolerance=±5% resistance=10k package=THT]
  S1 = Toggle Switch [package=THT]
  D1 = Zener Diode [part_number=LM4040D201LPR breakdown_voltage=2.05V package="300 mil [THT]"]
  R3 = Resistor [tolerance=±5% resistance=100k package=THT]
  R4 = Resistor [tolerance=±5% resistance=10k package=THT]
  U2 = LM124-324 Quad Opamp [package="DIP (Dual Inline)"]
  IC1 = IC, DIP package, 8 pins [chip_label=IC]
  C1 = Ceramic Capacitor [capacitance=100nF package="100 mil [THT, multilayer]"]
  C2 = Ceramic Capacitor [capacitance=100nF package="100 mil [THT, multilayer]"]
  R7 = Resistor [tolerance=±5% resistance=100k package=THT]
  R8 = Resistor [tolerance=±5% resistance=100k package=THT]
  R6 = Resistor [tolerance=±5% resistance=68k package=THT]
  R9 = Resistor [tolerance=±5% resistance=220k package=THT]
  R10 = Resistor [tolerance=±5% resistance=220k package=THT]
  D2 = Zener Diode [part_number=1N4732A breakdown_voltage=4.09V package="300 mil [THT]"]
  P2 = Power Jack [package=power_jack_slot]
  R5 = Resistor [tolerance=±5% resistance=10k package=THT]

nets:
  N1: U1.E, U1.A, S1.COM, R3.Pin_0, R4.Pin_0, U2.VCC+, R10.Pin_0
  N2: U1.C, R2.Pin_0, IC1.pin1
  N3: U1.K, R1.Pin_1
  GND: R1.Pin_0, R2.Pin_1, D1.anode, U2.VCC-, P2.GNDBREAK
  N4: S1.L2, P2.PWR
  N5: D1.cathode, R3.Pin_1, U2.4IN+, D2.anode
  N6: R4.Pin_1, U2.3IN+, D2.cathode
  N7: U2.2IN+, R7.Pin_0
  N8: U2.2IN-, R8.Pin_1, R9.Pin_0, R10.Pin_1
  N9: U2.2OUT, R9.Pin_1
  N10: U2.3OUT, U2.3IN-, IC1.pin5, IC1.pin6
  N11: U2.4IN-, U2.4OUT, IC1.pin8, C1.0, C2.0, R8.Pin_0, R6.Pin_1, R5.Pin_0
  N12: IC1.pin2, C1.1
  N13: IC1.pin3, C2.1, R6.Pin_0
  N14: IC1.pin4, IC1.pin7, R7.Pin_1, R5.Pin_1

notes:
  Out
  V+
  V-
  -
  +
